# Fritzing sketch rover (saved by Fritzing 0.7.11b)
stripboards: 1

parts:
  XTAL1 = Crystal [frequency="16 Mhz" package=THT]
  C1 = Ceramic Capacitor [capacitance=22pF package="100 mil [THT, multilayer]"]
  C2 = Ceramic Capacitor [capacitance=22pF package="100 mil [THT, multilayer]"]
  C3 = Ceramic Capacitor [capacitance=100nF package="100 mil [THT, multilayer]"]
  C5 = Electrolytic Capacitor [capacitance=10µF package="100 mil [THT, electrolytic]"]
  C6 = Ceramic Capacitor [capacitance=100nF package="100 mil [THT, multilayer]"]
  IC1 = H-Bridge [package=THT]
  J3 = male pin header, 2 pins [form="♂ (male)"]
  J4 = male pin header, 2 pins [form="♂ (male)"]
  C8 = Electrolytic Capacitor [capacitance=10µF package="100 mil [THT, electrolytic]"]
  C4 = Ceramic Capacitor [capacitance=100nF package="100 mil [THT, multilayer]"]
  U1 = atmega328 [package="DIP28 (Dual Inline) [THT]"]
  J5 = male pin header, 6 pins [form="♂ (male)"]
  C9 = Ceramic Capacitor [capacitance=100nF package="100 mil [THT, multilayer]"]
  S1 = Toggle Switch [package=THT]
  LED1 = LED - 5mm [color="Green (555nm)" package="5 mm [THT]"]
  R1 = Resistor [tolerance=±5% resistance=220 package=THT]
  LED2 = LED - 5mm [color="Red (633nm)" package="5 mm [THT]"]
  Power_plug1 = Power plug
  U2 = Voltage Regulator - 5V [package="TO220 [THT]"]
  R2 = Resistor [tolerance=±5% resistance=220 package=THT]

nets:
  N1: XTAL1.pin_0, C1.1, U1.XLAT1
  N2: XTAL1.pin_1, C2.1, U1.XLAT2
  GND: C1.0, C2.0, C3.0, C5.-, C6.0, IC1.GND1, IC1.GND2, IC1.GND3, IC1.GND4, C8.-, C4.0, U1.GND, J5.pin1, R1.Pin_0, Power_plug1.GND, U2.GND, R2.Pin_0
  Vout: C3.1, C5.+, IC1.VCC1, C4.1, U1.VCC, U1.AVCC, J5.pin3, LED2.anode, U2.output_voltage
  N3: C6.1, U1.AREF
  M2EN: IC1.1_2EN, U1.D3_(PWM)
  M2B: IC1.1A, U1.D2
  N4: IC1.1Y, J4.pin2
  N5: IC1.2Y, J4.pin1
  M2A: IC1.2A, U1.D4
  Vin: IC1.VCC2, C8.+, S1.COM, S1.L2, U2.input_voltage
  M1EN: IC1.3_4EN, U1.D6_(PWM)
  M1B: IC1.3A, U1.D7
  N6: IC1.3Y, J3.pin2
  N7: IC1.4Y, J3.pin1
  M1A: IC1.4A, U1.D8
  N8: U1.RESET, C9.1
  N9: U1.D0_(RX), J5.pin4
  N10: U1.D1_(TX), J5.pin5
  N11: U1.D13, LED1.anode
  N12: J5.pin6, C9.0
  N13: S1.L1, Power_plug1.VCC
  N14: LED1.cathode, R1.Pin_1
  N15: LED2.cathode, R2.Pin_1
